// Logisim project scheme.circ as structural Verilog: 20 circuits, main circuit main
module main (
);

  wire and_1_out, cdm_16_1_p2, cdm_16_1_p3, clk, in, mem, not_1_out, not_2_out, or_1_out, out, pc_move,
       player_move, read, word;
  wire [3:0] randctrl1_1_out, randctrl2_1_out;
  wire [6:0] keyboard_1_data;
  wire [15:0] addr_bus, bit_extender_1_out, cdm_16_1_p9, cdm_16_1_p10, data_bus, mem_wrap_1_bus_0,
       mem_wrap_1_bus_1, mem_wrap_2_bus_0, mem_wrap_2_bus_1;
  wire [31:0] controller32black_1_out_5, controller32black_1_out_6, controller32black_1_out_7,
       controller32black_1_out_8, controller32black_1_out_9, controller32black_1_out_10,
       controller32black_1_out_11, controller32black_1_out_12, controller32black_1_out_13,
       controller32black_1_out_14, controller32black_1_out_15, controller32black_1_out_16,
       controller32black_1_out_17, controller32black_1_out_18, controller32black_1_out_19,
       controller32black_1_out_20, controller32black_1_out_21, controller32black_1_out_22,
       controller32black_1_out_23, controller32black_1_out_24, controller32black_1_out_25,
       controller32black_1_out_26, controller32black_1_out_27, controller32black_1_out_28,
       controller32black_1_out_29, controller32white_1_out_5, controller32white_1_out_6,
       controller32white_1_out_7, controller32white_1_out_8, controller32white_1_out_9,
       controller32white_1_out_10, controller32white_1_out_11, controller32white_1_out_12,
       controller32white_1_out_13, controller32white_1_out_14, controller32white_1_out_15,
       controller32white_1_out_16, controller32white_1_out_17, controller32white_1_out_18,
       controller32white_1_out_19, controller32white_1_out_20, controller32white_1_out_21,
       controller32white_1_out_22, controller32white_1_out_23, controller32white_1_out_24,
       controller32white_1_out_25, controller32white_1_out_26, controller32white_1_out_27,
       controller32white_1_out_28, controller32white_1_out_29;

  Clock clock_1 (.out(clk));
  // Probe on cdm_16_1_p2
  // CdM_16 cdm_16_1: pin names not known; wires that end beside it: clk, cdm_16_1_p2, cdm_16_1_p3, clk, mem, read, word, addr_bus, cdm_16_1_p9, cdm_16_1_p10
  // Debugger debugger_1: pin names not known
  // Probe on cdm_16_1_p3
  // Probe on addr_bus
  assign data_bus = not_1_out ? cdm_16_1_p9 : 16'bz;  // Controlled_Buffer controlled_buffer_1
  not not_1 (not_1_out, read);
  assign cdm_16_1_p10 = read ? data_bus : 16'bz;  // Controlled_Buffer controlled_buffer_2
  DotMatrix #(.matrixcols(25), .matrixrows(20)) dotmatrix_1 (
    .col0({20{1'b0}}), .col1(20'h1ffe), .col2({20{1'b0}}), .col3(20'h1ffe), .col4({20{1'b0}}),
    .col5(20'h1ffe), .col6({20{1'b0}}), .col7(20'h1ffe), .col8({20{1'b0}}), .col9(20'h1ffe),
    .col10({20{1'b0}}), .col11(20'h1ffe), .col12({20{1'b0}}), .col13(20'h1ffe), .col14({20{1'b0}}),
    .col15(20'h1ffe), .col16({20{1'b0}}), .col17(20'h1ffe), .col18({20{1'b0}}), .col19(20'h1ffe),
    .col20({20{1'b0}}), .col21(20'h1ffe), .col22({20{1'b0}}), .col23(20'h1ffe), .col24({20{1'b0}}));
  DotMatrix #(.matrixcols(25), .matrixrows(32), .dotshape("circle")) dotmatrix_2 (
    .col0(controller32white_1_out_5), .col1(controller32white_1_out_18), .col2(controller32white_1_out_6),
    .col3(controller32white_1_out_19), .col4(controller32white_1_out_7), .col5(controller32white_1_out_20),
    .col6(controller32white_1_out_8), .col7(controller32white_1_out_21), .col8(controller32white_1_out_9),
    .col9(controller32white_1_out_22), .col10(controller32white_1_out_10),
    .col11(controller32white_1_out_23), .col12(controller32white_1_out_11),
    .col13(controller32white_1_out_24), .col14(controller32white_1_out_12),
    .col15(controller32white_1_out_25), .col16(controller32white_1_out_13),
    .col17(controller32white_1_out_26), .col18(controller32white_1_out_14),
    .col19(controller32white_1_out_27), .col20(controller32white_1_out_15),
    .col21(controller32white_1_out_28), .col22(controller32white_1_out_16),
    .col23(controller32white_1_out_29), .col24(controller32white_1_out_17));
  DotMatrix #(.matrixcols(25), .matrixrows(32), .dotshape("circle")) dotmatrix_3 (
    .col0(controller32black_1_out_5), .col1(controller32black_1_out_18), .col2(controller32black_1_out_6),
    .col3(controller32black_1_out_19), .col4(controller32black_1_out_7), .col5(controller32black_1_out_20),
    .col6(controller32black_1_out_8), .col7(controller32black_1_out_21), .col8(controller32black_1_out_9),
    .col9(controller32black_1_out_22), .col10(controller32black_1_out_10),
    .col11(controller32black_1_out_23), .col12(controller32black_1_out_11),
    .col13(controller32black_1_out_24), .col14(controller32black_1_out_12),
    .col15(controller32black_1_out_25), .col16(controller32black_1_out_13),
    .col17(controller32black_1_out_26), .col18(controller32black_1_out_14),
    .col19(controller32black_1_out_27), .col20(controller32black_1_out_15),
    .col21(controller32black_1_out_28), .col22(controller32black_1_out_16),
    .col23(controller32black_1_out_29), .col24(controller32black_1_out_17));
  DotMatrix #(.matrixcols(25), .matrixrows(20)) dotmatrix_4 (
    .col0({20{1'b0}}), .col1(20'h7ff80), .col2({20{1'b0}}), .col3(20'h7ff80), .col4({20{1'b0}}),
    .col5(20'h7ff80), .col6({20{1'b0}}), .col7(20'h7ff80), .col8({20{1'b0}}), .col9(20'h7ff80),
    .col10({20{1'b0}}), .col11(20'h7ff80), .col12({20{1'b0}}), .col13(20'h7ff80), .col14({20{1'b0}}),
    .col15(20'h7ff80), .col16({20{1'b0}}), .col17(20'h7ff80), .col18({20{1'b0}}), .col19(20'h7ff80),
    .col20({20{1'b0}}), .col21(20'h7ff80), .col22({20{1'b0}}), .col23(20'h7ff80), .col24({20{1'b0}}));
  // Probe on data_bus
  controller32white controller32white_1 (
    .column(mem_wrap_1_bus_1), .value(mem_wrap_1_bus_0), .out_5(controller32white_1_out_5),
    .out_6(controller32white_1_out_6), .out_7(controller32white_1_out_7), .out_8(controller32white_1_out_8),
    .out_9(controller32white_1_out_9), .out_10(controller32white_1_out_10),
    .out_11(controller32white_1_out_11), .out_12(controller32white_1_out_12),
    .out_13(controller32white_1_out_13), .out_14(controller32white_1_out_14),
    .out_15(controller32white_1_out_15), .out_16(controller32white_1_out_16),
    .out_17(controller32white_1_out_17), .clk(clk), .out_18(controller32white_1_out_18),
    .out_19(controller32white_1_out_19), .out_20(controller32white_1_out_20),
    .out_21(controller32white_1_out_21), .out_22(controller32white_1_out_22),
    .out_23(controller32white_1_out_23), .out_24(controller32white_1_out_24),
    .out_25(controller32white_1_out_25), .out_26(controller32white_1_out_26),
    .out_27(controller32white_1_out_27), .out_28(controller32white_1_out_28),
    .out_29(controller32white_1_out_29), .write(player_move));
  controller32black controller32black_1 (
    .clk(clk), .write(pc_move), .column(mem_wrap_2_bus_1), .value(mem_wrap_2_bus_0),
    .out_5(controller32black_1_out_5), .out_6(controller32black_1_out_6), .out_7(controller32black_1_out_7),
    .out_8(controller32black_1_out_8), .out_9(controller32black_1_out_9),
    .out_10(controller32black_1_out_10), .out_11(controller32black_1_out_11),
    .out_12(controller32black_1_out_12), .out_13(controller32black_1_out_13),
    .out_14(controller32black_1_out_14), .out_15(controller32black_1_out_15),
    .out_16(controller32black_1_out_16), .out_17(controller32black_1_out_17),
    .out_18(controller32black_1_out_18), .out_24(controller32black_1_out_24),
    .out_19(controller32black_1_out_19), .out_25(controller32black_1_out_25),
    .out_20(controller32black_1_out_20), .out_26(controller32black_1_out_26),
    .out_21(controller32black_1_out_21), .out_27(controller32black_1_out_27),
    .out_22(controller32black_1_out_22), .out_28(controller32black_1_out_28),
    .out_23(controller32black_1_out_23), .out_29(controller32black_1_out_29));
  and and_1 (and_1_out, mem, not_2_out);
  not not_2 (not_2_out, in);
  MEM_WRAP mem_wrap_1 (
    .addr_bus(addr_bus), .data_bus(data_bus), .clk(clk), .bus_0(mem_wrap_1_bus_0), .bus_1(mem_wrap_1_bus_1),
    .read(read));
  MEM_WRAP mem_wrap_2 (
    .addr_bus(addr_bus), .data_bus(data_bus), .clk(clk), .bus_0(mem_wrap_2_bus_0), .bus_1(mem_wrap_2_bus_1),
    .read(read));
  // RAM ram_1: pin names not known; wires that end beside it: addr_bus, word, and_1_out, clk, read, data_bus
  Hex_Digit_Display hex_digit_display_1 (.value(randctrl1_1_out));  // open: dp
  randctrl1 randctrl1_1 (
    .addr_bus(addr_bus), .data_bus(data_bus), .mem(mem), .read(read), .clk(clk), .out(randctrl1_1_out));
  TTY #(.cols(40)) tty_1 (.data(data_bus[6:0]), .clk(clk), .we(or_1_out));  // open: clr
  Hex_Digit_Display hex_digit_display_2 (.value(randctrl2_1_out));  // open: dp
  randctrl2 randctrl2_1 (
    .addr_bus(addr_bus), .data_bus(data_bus), .mem(mem), .read(read), .clk(clk), .out(randctrl2_1_out));
  or or_1 (or_1_out, in, out);
  Keyboard #(.trigger("falling")) keyboard_1 (.clk(clk), .re(in), .data(keyboard_1_data));  // open: clr, avail
  turn_changer turn_changer_1 (
    .data_bus(data_bus), .address_bus(addr_bus), .address(16'hff4a), .memory(mem), .read(read), .clk(clk),
    .player(pc_move), .pc(player_move));
  assign bit_extender_1_out = {{9{1'b0}}, keyboard_1_data};  // Bit_Extender bit_extender_1
  assign data_bus = in ? bit_extender_1_out : 16'bz;  // Controlled_Buffer controlled_buffer_3
  OUT_CTRL out_ctrl_1 (.addr_bus(addr_bus), .mem(mem), .read(read), .bus_0(out));
  IN_CTRL in_ctrl_1 (.addr_bus(addr_bus), .mem(mem), .read(read), .bus_0(in));
endmodule

module controller32white (
  input  clk,
  input  write,
  input  [15:0] column,
  input  [15:0] value,
  output [31:0] out_5,
  output [31:0] out_6,
  output [31:0] out_7,
  output [31:0] out_8,
  output [31:0] out_9,
  output [31:0] out_10,
  output [31:0] out_11,
  output [31:0] out_12,
  output [31:0] out_13,
  output [31:0] out_14,
  output [31:0] out_15,
  output [31:0] out_16,
  output [31:0] out_17,
  output [31:0] out_18,
  output [31:0] out_19,
  output [31:0] out_20,
  output [31:0] out_21,
  output [31:0] out_22,
  output [31:0] out_23,
  output [31:0] out_24,
  output [31:0] out_25,
  output [31:0] out_26,
  output [31:0] out_27,
  output [31:0] out_28,
  output [31:0] out_29
);

  wire and_1_out, and_2_out, and_3_out, and_4_out, and_5_out, and_6_out, and_7_out, and_8_out, and_9_out,
       and_10_out, and_11_out, and_12_out, and_13_out, and_14_out, and_15_out, and_16_out, and_17_out,
       and_18_out, and_19_out, and_20_out, and_21_out, and_22_out, and_23_out, and_24_out;
  wire [15:0] shifter_bot_white_1_out, shifter_bot_white_2_out, shifter_bot_white_3_out,
       shifter_bot_white_4_out, shifter_bot_white_5_out, shifter_bot_white_6_out, shifter_bot_white_7_out,
       shifter_bot_white_8_out, shifter_bot_white_9_out, shifter_bot_white_10_out, shifter_bot_white_11_out,
       shifter_bot_white_12_out, shifter_top_white_1_out, shifter_top_white_2_out, shifter_top_white_3_out,
       shifter_top_white_4_out, shifter_top_white_5_out, shifter_top_white_6_out, shifter_top_white_7_out,
       shifter_top_white_8_out, shifter_top_white_9_out, shifter_top_white_10_out, shifter_top_white_11_out,
       shifter_top_white_12_out;

  shifter_bot_white shifter_bot_white_1 (.in(value), .out(shifter_bot_white_1_out));
  and and_1 (and_1_out, ~column[0], column[1], write);  // AND_Gate
  shifter_top_white shifter_top_white_1 (.in(value), .out(shifter_top_white_1_out));
  and and_2 (and_2_out, column[0], column[1], write);
  shifter_bot_white shifter_bot_white_2 (.in(value), .out(shifter_bot_white_2_out));
  and and_3 (and_3_out, ~column[0], column[7], write);  // AND_Gate
  shifter_top_white shifter_top_white_2 (.in(value), .out(shifter_top_white_2_out));
  and and_4 (and_4_out, column[0], column[7], write);
  Register #(.width(16), .trigger("falling")) reg_bot (
    .D(shifter_bot_white_1_out), .en(and_1_out), .Q(out_18[15:0]), .clk(clk));  // open: clr
  Register #(.width(16), .trigger("falling")) reg_top (
    .D(shifter_top_white_1_out), .en(and_2_out), .Q(out_18[31:16]), .clk(clk));  // open: clr
  Register #(.width(16), .trigger("falling")) reg_bot_2 (
    .D(shifter_bot_white_2_out), .en(and_3_out), .Q(out_24[15:0]), .clk(clk));  // open: clr
  Register #(.width(16), .trigger("falling")) reg_top_2 (
    .D(shifter_top_white_2_out), .en(and_4_out), .Q(out_24[31:16]), .clk(clk));  // open: clr
  shifter_bot_white shifter_bot_white_3 (.in(value), .out(shifter_bot_white_3_out));
  and and_5 (and_5_out, ~column[0], column[2], write);  // AND_Gate
  shifter_top_white shifter_top_white_3 (.in(value), .out(shifter_top_white_3_out));
  and and_6 (and_6_out, column[0], column[2], write);
  shifter_bot_white shifter_bot_white_4 (.in(value), .out(shifter_bot_white_4_out));
  and and_7 (and_7_out, ~column[0], column[8], write);  // AND_Gate
  shifter_top_white shifter_top_white_4 (.in(value), .out(shifter_top_white_4_out));
  and and_8 (and_8_out, column[0], column[8], write);
  Register #(.width(16), .trigger("falling")) reg_bot_3 (
    .D(shifter_bot_white_3_out), .en(and_5_out), .Q(out_19[15:0]), .clk(clk));  // open: clr
  Register #(.width(16), .trigger("falling")) reg_top_3 (
    .D(shifter_top_white_3_out), .en(and_6_out), .Q(out_19[31:16]), .clk(clk));  // open: clr
  Register #(.width(16), .trigger("falling")) reg_bot_4 (
    .D(shifter_bot_white_4_out), .en(and_7_out), .Q(out_25[15:0]), .clk(clk));  // open: clr
  Register #(.width(16), .trigger("falling")) reg_top_4 (
    .D(shifter_top_white_4_out), .en(and_8_out), .Q(out_25[31:16]), .clk(clk));  // open: clr
  shifter_bot_white shifter_bot_white_5 (.in(value), .out(shifter_bot_white_5_out));
  and and_9 (and_9_out, ~column[0], column[3], write);  // AND_Gate
  shifter_top_white shifter_top_white_5 (.in(value), .out(shifter_top_white_5_out));
  and and_10 (and_10_out, column[0], column[3], write);
  shifter_bot_white shifter_bot_white_6 (.in(value), .out(shifter_bot_white_6_out));
  and and_11 (and_11_out, ~column[0], column[9], write);  // AND_Gate
  shifter_top_white shifter_top_white_6 (.in(value), .out(shifter_top_white_6_out));
  and and_12 (and_12_out, column[0], column[9], write);
  Register #(.width(16), .trigger("falling")) reg_bot_5 (
    .D(shifter_bot_white_5_out), .en(and_9_out), .Q(out_20[15:0]), .clk(clk));  // open: clr
  Register #(.width(16), .trigger("falling")) reg_top_5 (
    .D(shifter_top_white_5_out), .en(and_10_out), .Q(out_20[31:16]), .clk(clk));  // open: clr
  Register #(.width(16), .trigger("falling")) reg_bot_6 (
    .D(shifter_bot_white_6_out), .en(and_11_out), .Q(out_26[15:0]), .clk(clk));  // open: clr
  Register #(.width(16), .trigger("falling")) reg_top_6 (
    .D(shifter_top_white_6_out), .en(and_12_out), .Q(out_26[31:16]), .clk(clk));  // open: clr
  shifter_bot_white shifter_bot_white_7 (.in(value), .out(shifter_bot_white_7_out));
  and and_13 (and_13_out, ~column[0], column[4], write);  // AND_Gate
  shifter_top_white shifter_top_white_7 (.in(value), .out(shifter_top_white_7_out));
  and and_14 (and_14_out, column[0], column[4], write);
  shifter_bot_white shifter_bot_white_8 (.in(value), .out(shifter_bot_white_8_out));
  and and_15 (and_15_out, ~column[0], column[10], write);  // AND_Gate
  shifter_top_white shifter_top_white_8 (.in(value), .out(shifter_top_white_8_out));
  and and_16 (and_16_out, column[0], column[10], write);
  Register #(.width(16), .trigger("falling")) reg_bot_7 (
    .D(shifter_bot_white_7_out), .en(and_13_out), .Q(out_21[15:0]), .clk(clk));  // open: clr
  Register #(.width(16), .trigger("falling")) reg_top_7 (
    .D(shifter_top_white_7_out), .en(and_14_out), .Q(out_21[31:16]), .clk(clk));  // open: clr
  Register #(.width(16), .trigger("falling")) reg_bot_8 (
    .D(shifter_bot_white_8_out), .en(and_15_out), .Q(out_27[15:0]), .clk(clk));  // open: clr
  Register #(.width(16), .trigger("falling")) reg_top_8 (
    .D(shifter_top_white_8_out), .en(and_16_out), .Q(out_27[31:16]), .clk(clk));  // open: clr
  shifter_bot_white shifter_bot_white_9 (.in(value), .out(shifter_bot_white_9_out));
  and and_17 (and_17_out, ~column[0], column[5], write);  // AND_Gate
  shifter_top_white shifter_top_white_9 (.in(value), .out(shifter_top_white_9_out));
  and and_18 (and_18_out, column[0], column[5], write);
  shifter_bot_white shifter_bot_white_10 (.in(value), .out(shifter_bot_white_10_out));
  and and_19 (and_19_out, ~column[0], column[11], write);  // AND_Gate
  shifter_top_white shifter_top_white_10 (.in(value), .out(shifter_top_white_10_out));
  and and_20 (and_20_out, column[0], column[11], write);
  Register #(.width(16), .trigger("falling")) reg_bot_9 (
    .D(shifter_bot_white_9_out), .en(and_17_out), .Q(out_22[15:0]), .clk(clk));  // open: clr
  Register #(.width(16), .trigger("falling")) reg_top_9 (
    .D(shifter_top_white_9_out), .en(and_18_out), .Q(out_22[31:16]), .clk(clk));  // open: clr
  Register #(.width(16), .trigger("falling")) reg_bot_10 (
    .D(shifter_bot_white_10_out), .en(and_19_out), .Q(out_28[15:0]), .clk(clk));  // open: clr
  Register #(.width(16), .trigger("falling")) reg_top_10 (
    .D(shifter_top_white_10_out), .en(and_20_out), .Q(out_28[31:16]), .clk(clk));  // open: clr
  Register #(.width(16), .trigger("falling")) reg_bot_11 (
    .D(shifter_bot_white_11_out), .en(and_21_out), .Q(out_23[15:0]), .clk(clk));  // open: clr
  shifter_bot_white shifter_bot_white_11 (.in(value), .out(shifter_bot_white_11_out));
  and and_21 (and_21_out, ~column[0], column[6], write);  // AND_Gate
  shifter_top_white shifter_top_white_11 (.in(value), .out(shifter_top_white_11_out));
  Register #(.width(16), .trigger("falling")) reg_top_11 (
    .D(shifter_top_white_11_out), .en(and_22_out), .Q(out_23[31:16]), .clk(clk));  // open: clr
  and and_22 (and_22_out, column[0], column[6], write);
  shifter_bot_white shifter_bot_white_12 (.in(value), .out(shifter_bot_white_12_out));
  Register #(.width(16), .trigger("falling")) reg_bot_12 (
    .D(shifter_bot_white_12_out), .en(and_23_out), .Q(out_29[15:0]), .clk(clk));  // open: clr
  and and_23 (and_23_out, ~column[0], column[12], write);  // AND_Gate
  shifter_top_white shifter_top_white_12 (.in(value), .out(shifter_top_white_12_out));
  Register #(.width(16), .trigger("falling")) reg_top_12 (
    .D(shifter_top_white_12_out), .en(and_24_out), .Q(out_29[31:16]), .clk(clk));  // open: clr
  and and_24 (and_24_out, column[0], column[12], write);

  assign out_5 = {32{1'b0}};
  assign out_6 = {32{1'b0}};
  assign out_7 = {32{1'b0}};
  assign out_8 = {32{1'b0}};
  assign out_9 = {32{1'b0}};
  assign out_10 = {32{1'b0}};
  assign out_11 = {32{1'b0}};
  assign out_12 = {32{1'b0}};
  assign out_13 = {32{1'b0}};
  assign out_14 = {32{1'b0}};
  assign out_15 = {32{1'b0}};
  assign out_16 = {32{1'b0}};
  assign out_17 = {32{1'b0}};

  // Other names for the same wires on the sheet: column_t = column[0]; _1_COL = column[1]; _2_COL = column[2];
  //   _3_COL = column[3]; _4_COL = column[4]; _5_COL = column[5]; _6_COL = column[6]; _7_COL = column[7];
  //   _8_COL = column[8]; _9_COL = column[9]; _10_COL = column[10]; _11_COL = column[11]; _12_COL = column[12];
  //   DATA[15:0] = value; w = write

  // Notes on the sheet:
  //   0 - bot, 1 - top
endmodule

module turn_changer (
  input  [15:0] data_bus,
  input  [15:0] address_bus,
  input  [15:0] address,
  input  memory,
  input  read,
  input  clk,
  output player,
  output pc
);

  wire and_1_out, comparator_1_a___b;
  wire [15:0] register_1_q;

  Comparator comparator_1 (.A(address_bus), .B(address), .A___B(comparator_1_a___b));  // open: A___B_2, A___B_3
  and and_1 (and_1_out, comparator_1_a___b, memory, ~read);  // AND_Gate
  Register #(.width(16)) register_1 (.D(data_bus), .en(and_1_out), .Q(register_1_q), .clk(clk));  // open: clr
  and and_2 (player, ~register_1_q[0], ~register_1_q[7]);  // AND_Gate
  and and_3 (pc, register_1_q[0], ~register_1_q[7]);  // AND_Gate
endmodule

module value_converter (
  input  [3:0] value,
  output [15:0] out
);

  ROM #(.addrWidth(4), .dataWidth(16)) rom_1 (.addr(value), .data(out));  // open: sel

  // Notes on the sheet:
  //   contents of rom_1 (hex, n*v repeats v):
  //   0 1 3 7 f 1f 3f 7f ff 1ff 3ff 7ff fff
endmodule

module MEM_WRAP (
  input  [15:0] addr_bus,
  input  [15:0] data_bus,
  input  clk,
  input  read,
  output [15:0] bus_0,
  output [15:0] bus_1
);

  wire and_1_out, and_2_out, comparator_1_a___b_3, comparator_2_a___b, subtractor_1_bout;
  wire [15:0] register_1_q, register_2_q, shifter_1_out, subtractor_1_out;

  // Probe on addr_bus
  Subtractor #(.width(16)) subtractor_1 (
    .a(addr_bus), .b(16'hff00), .out(subtractor_1_out), .bout(subtractor_1_bout));  // open: bin
  Comparator comparator_1 (.A(subtractor_1_out), .B(16'h32), .A___B_3(comparator_1_a___b_3));  // open: A___B, A___B_2
  Comparator comparator_2 (.A(addr_bus), .B(16'hff4a), .A___B(comparator_2_a___b));  // open: A___B_2, A___B_3
  and and_1 (and_1_out, comparator_2_a___b, ~read);  // AND_Gate
  Shifter #(.width(16), .shift("ar")) shifter_1 (.in(subtractor_1_out), .\dist (4'b0001), .out(shifter_1_out));
  Register #(.width(16), .trigger("falling")) register_1 (
    .D(data_bus), .en(and_2_out), .Q(register_1_q), .clk(clk), .clr(and_1_out));
  and and_2 (and_2_out, comparator_1_a___b_3, ~subtractor_1_bout);  // AND_Gate
  // Probe on register_1_q[3:0]
  // Probe on register_2_q[4:0]
  Register #(.width(16), .trigger("falling")) register_2 (
    .D(shifter_1_out), .en(and_2_out), .Q(register_2_q), .clk(clk), .clr(and_1_out));
  value_converter value_converter_1 (.value(register_1_q[3:0]), .out(bus_0));
  column_converter column_converter_1 (.in(register_2_q[4:0]), .out(bus_1));
endmodule

module column_converter (
  input  [4:0] in,
  output [15:0] out
);

  // Probe on in
  ROM #(.addrWidth(5), .dataWidth(16)) rom_1 (.addr(in), .data(out));  // open: sel

  // Notes on the sheet:
  //   contents of rom_1 (hex, n*v repeats v):
  //   0 2 4 8 10 20 40 80 100 200 400 800 1000 1001 801 401 201 101 81 41 21 11 9 5 3
endmodule

module inverter (
  input  [15:0] in,
  output [15:0] out
);


  assign out = {in[0], in[1], in[2], in[3], in[4], in[5], in[6], in[7], in[8], in[9], in[10], in[11], in[12], in[13], in[14], in[15]};
endmodule

module shifter_top_white (
  input  [15:0] in,
  output [15:0] out
);

  wire [15:0] inverter_1_out;

  inverter inverter_1 (.in(in), .out(inverter_1_out));
  Shifter #(.width(16), .shift("lr")) shifter_1 (.in(inverter_1_out), .\dist (4'b0101), .out(out));
endmodule

module shifter_bot_white (
  input  [15:0] in,
  output [15:0] out
);

  Shifter #(.width(16)) shifter_1 (.in(in), .\dist (4'b0001), .out(out));
endmodule

module controller32black (
  input  clk,
  input  write,
  input  [15:0] column,
  input  [15:0] value,
  output [31:0] out_5,
  output [31:0] out_6,
  output [31:0] out_7,
  output [31:0] out_8,
  output [31:0] out_9,
  output [31:0] out_10,
  output [31:0] out_11,
  output [31:0] out_12,
  output [31:0] out_13,
  output [31:0] out_14,
  output [31:0] out_15,
  output [31:0] out_16,
  output [31:0] out_17,
  output [31:0] out_18,
  output [31:0] out_19,
  output [31:0] out_20,
  output [31:0] out_21,
  output [31:0] out_22,
  output [31:0] out_23,
  output [31:0] out_24,
  output [31:0] out_25,
  output [31:0] out_26,
  output [31:0] out_27,
  output [31:0] out_28,
  output [31:0] out_29
);

  wire and_1_out, and_2_out, and_3_out, and_4_out, and_5_out, and_6_out, and_7_out, and_8_out, and_9_out,
       and_10_out, and_11_out, and_12_out, and_13_out, and_14_out, and_15_out, and_16_out, and_17_out,
       and_18_out, and_19_out, and_20_out, and_21_out, and_22_out, and_23_out, and_24_out;
  wire [15:0] shifter_bot_black_1_out, shifter_bot_black_2_out, shifter_bot_black_3_out,
       shifter_bot_black_4_out, shifter_bot_black_5_out, shifter_bot_black_6_out, shifter_bot_black_7_out,
       shifter_bot_black_8_out, shifter_bot_black_9_out, shifter_bot_black_10_out, shifter_bot_black_11_out,
       shifter_bot_black_12_out, shifter_top_black_1_out, shifter_top_black_2_out, shifter_top_black_3_out,
       shifter_top_black_4_out, shifter_top_black_5_out, shifter_top_black_6_out, shifter_top_black_7_out,
       shifter_top_black_8_out, shifter_top_black_9_out, shifter_top_black_10_out, shifter_top_black_11_out,
       shifter_top_black_12_out;

  shifter_bot_black shifter_bot_black_1 (.in(value), .out(shifter_bot_black_1_out));
  and and_1 (and_1_out, ~column[0], column[1], write);  // AND_Gate
  shifter_top_black shifter_top_black_1 (.in(value), .out(shifter_top_black_1_out));
  and and_2 (and_2_out, column[0], column[1], write);
  shifter_bot_black shifter_bot_black_2 (.in(value), .out(shifter_bot_black_2_out));
  and and_3 (and_3_out, ~column[0], column[7], write);  // AND_Gate
  shifter_top_black shifter_top_black_2 (.in(value), .out(shifter_top_black_2_out));
  and and_4 (and_4_out, column[0], column[7], write);
  Register #(.width(16)) reg_bot (
    .D(shifter_bot_black_1_out), .en(and_1_out), .Q(out_18[15:0]), .clk(clk));  // open: clr
  Register #(.width(16)) reg_top (
    .D(shifter_top_black_1_out), .en(and_2_out), .Q(out_18[31:16]), .clk(clk));  // open: clr
  Register #(.width(16)) reg_bot_2 (
    .D(shifter_bot_black_2_out), .en(and_3_out), .Q(out_24[15:0]), .clk(clk));  // open: clr
  Register #(.width(16)) reg_top_2 (
    .D(shifter_top_black_2_out), .en(and_4_out), .Q(out_24[31:16]), .clk(clk));  // open: clr
  shifter_bot_black shifter_bot_black_3 (.in(value), .out(shifter_bot_black_3_out));
  and and_5 (and_5_out, ~column[0], column[2], write);  // AND_Gate
  shifter_top_black shifter_top_black_3 (.in(value), .out(shifter_top_black_3_out));
  and and_6 (and_6_out, column[0], column[2], write);
  shifter_bot_black shifter_bot_black_4 (.in(value), .out(shifter_bot_black_4_out));
  and and_7 (and_7_out, ~column[0], column[8], write);  // AND_Gate
  shifter_top_black shifter_top_black_4 (.in(value), .out(shifter_top_black_4_out));
  and and_8 (and_8_out, column[0], column[8], write);
  Register #(.width(16)) reg_bot_3 (
    .D(shifter_bot_black_3_out), .en(and_5_out), .Q(out_19[15:0]), .clk(clk));  // open: clr
  Register #(.width(16)) reg_top_3 (
    .D(shifter_top_black_3_out), .en(and_6_out), .Q(out_19[31:16]), .clk(clk));  // open: clr
  Register #(.width(16)) reg_bot_4 (
    .D(shifter_bot_black_4_out), .en(and_7_out), .Q(out_25[15:0]), .clk(clk));  // open: clr
  Register #(.width(16)) reg_top_4 (
    .D(shifter_top_black_4_out), .en(and_8_out), .Q(out_25[31:16]), .clk(clk));  // open: clr
  shifter_bot_black shifter_bot_black_5 (.in(value), .out(shifter_bot_black_5_out));
  and and_9 (and_9_out, ~column[0], column[3], write);  // AND_Gate
  shifter_top_black shifter_top_black_5 (.in(value), .out(shifter_top_black_5_out));
  and and_10 (and_10_out, column[0], column[3], write);
  shifter_bot_black shifter_bot_black_6 (.in(value), .out(shifter_bot_black_6_out));
  and and_11 (and_11_out, ~column[0], column[9], write);  // AND_Gate
  shifter_top_black shifter_top_black_6 (.in(value), .out(shifter_top_black_6_out));
  and and_12 (and_12_out, column[0], column[9], write);
  Register #(.width(16)) reg_bot_5 (
    .D(shifter_bot_black_5_out), .en(and_9_out), .Q(out_20[15:0]), .clk(clk));  // open: clr
  Register #(.width(16)) reg_top_5 (
    .D(shifter_top_black_5_out), .en(and_10_out), .Q(out_20[31:16]), .clk(clk));  // open: clr
  Register #(.width(16)) reg_bot_6 (
    .D(shifter_bot_black_6_out), .en(and_11_out), .Q(out_26[15:0]), .clk(clk));  // open: clr
  Register #(.width(16)) reg_top_6 (
    .D(shifter_top_black_6_out), .en(and_12_out), .Q(out_26[31:16]), .clk(clk));  // open: clr
  shifter_bot_black shifter_bot_black_7 (.in(value), .out(shifter_bot_black_7_out));
  and and_13 (and_13_out, ~column[0], column[4], write);  // AND_Gate
  shifter_top_black shifter_top_black_7 (.in(value), .out(shifter_top_black_7_out));
  and and_14 (and_14_out, column[0], column[4], write);
  shifter_bot_black shifter_bot_black_8 (.in(value), .out(shifter_bot_black_8_out));
  and and_15 (and_15_out, ~column[0], column[10], write);  // AND_Gate
  shifter_top_black shifter_top_black_8 (.in(value), .out(shifter_top_black_8_out));
  and and_16 (and_16_out, column[0], column[10], write);
  Register #(.width(16)) reg_bot_7 (
    .D(shifter_bot_black_7_out), .en(and_13_out), .Q(out_21[15:0]), .clk(clk));  // open: clr
  Register #(.width(16)) reg_top_7 (
    .D(shifter_top_black_7_out), .en(and_14_out), .Q(out_21[31:16]), .clk(clk));  // open: clr
  Register #(.width(16)) reg_bot_8 (
    .D(shifter_bot_black_8_out), .en(and_15_out), .Q(out_27[15:0]), .clk(clk));  // open: clr
  Register #(.width(16)) reg_top_8 (
    .D(shifter_top_black_8_out), .en(and_16_out), .Q(out_27[31:16]), .clk(clk));  // open: clr
  shifter_bot_black shifter_bot_black_9 (.in(value), .out(shifter_bot_black_9_out));
  and and_17 (and_17_out, ~column[0], column[5], write);  // AND_Gate
  shifter_top_black shifter_top_black_9 (.in(value), .out(shifter_top_black_9_out));
  and and_18 (and_18_out, column[0], column[5], write);
  shifter_bot_black shifter_bot_black_10 (.in(value), .out(shifter_bot_black_10_out));
  and and_19 (and_19_out, ~column[0], column[11], write);  // AND_Gate
  shifter_top_black shifter_top_black_10 (.in(value), .out(shifter_top_black_10_out));
  and and_20 (and_20_out, column[0], column[11], write);
  Register #(.width(16)) reg_bot_9 (
    .D(shifter_bot_black_9_out), .en(and_17_out), .Q(out_22[15:0]), .clk(clk));  // open: clr
  Register #(.width(16)) reg_top_9 (
    .D(shifter_top_black_9_out), .en(and_18_out), .Q(out_22[31:16]), .clk(clk));  // open: clr
  Register #(.width(16)) reg_bot_10 (
    .D(shifter_bot_black_10_out), .en(and_19_out), .Q(out_28[15:0]), .clk(clk));  // open: clr
  Register #(.width(16)) reg_top_10 (
    .D(shifter_top_black_10_out), .en(and_20_out), .Q(out_28[31:16]), .clk(clk));  // open: clr
  Register #(.width(16)) reg_bot_11 (
    .D(shifter_bot_black_11_out), .en(and_21_out), .Q(out_23[15:0]), .clk(clk));  // open: clr
  shifter_bot_black shifter_bot_black_11 (.in(value), .out(shifter_bot_black_11_out));
  and and_21 (and_21_out, ~column[0], column[6], write);  // AND_Gate
  shifter_top_black shifter_top_black_11 (.in(value), .out(shifter_top_black_11_out));
  Register #(.width(16)) reg_top_11 (
    .D(shifter_top_black_11_out), .en(and_22_out), .Q(out_23[31:16]), .clk(clk));  // open: clr
  and and_22 (and_22_out, column[0], column[6], write);
  shifter_bot_black shifter_bot_black_12 (.in(value), .out(shifter_bot_black_12_out));
  Register #(.width(16)) reg_bot_12 (
    .D(shifter_bot_black_12_out), .en(and_23_out), .Q(out_29[15:0]), .clk(clk));  // open: clr
  and and_23 (and_23_out, ~column[0], column[12], write);  // AND_Gate
  shifter_top_black shifter_top_black_12 (.in(value), .out(shifter_top_black_12_out));
  Register #(.width(16)) reg_top_12 (
    .D(shifter_top_black_12_out), .en(and_24_out), .Q(out_29[31:16]), .clk(clk));  // open: clr
  and and_24 (and_24_out, column[0], column[12], write);

  assign out_5 = {32{1'b0}};
  assign out_6 = {32{1'b0}};
  assign out_7 = {32{1'b0}};
  assign out_8 = {32{1'b0}};
  assign out_9 = {32{1'b0}};
  assign out_10 = {32{1'b0}};
  assign out_11 = {32{1'b0}};
  assign out_12 = {32{1'b0}};
  assign out_13 = {32{1'b0}};
  assign out_14 = {32{1'b0}};
  assign out_15 = {32{1'b0}};
  assign out_16 = {32{1'b0}};
  assign out_17 = {32{1'b0}};

  // Other names for the same wires on the sheet: column_t = column[0]; _1_COL = column[1]; _2_COL = column[2];
  //   _3_COL = column[3]; _4_COL = column[4]; _5_COL = column[5]; _6_COL = column[6]; _7_COL = column[7];
  //   _8_COL = column[8]; _9_COL = column[9]; _10_COL = column[10]; _11_COL = column[11]; _12_COL = column[12];
  //   DATA[15:0] = value; w = write

  // Notes on the sheet:
  //   0 - bot, 1 - top
endmodule

module shifter_top_black (
  input  [15:0] in,
  output [15:0] out
);

  wire [15:0] inverter_1_out;

  inverter inverter_1 (.in(in), .out(inverter_1_out));
  Shifter #(.width(16), .shift("lr")) shifter_1 (.in(inverter_1_out), .\dist (4'b0010), .out(out));
endmodule

module shifter_bot_black (
  input  [15:0] in,
  output [15:0] out
);

  Shifter #(.width(16)) shifter_1 (.in(in), .\dist (4'b0100), .out(out));
endmodule

module OUT_CTRL (
  input  [15:0] addr_bus,
  input  mem,
  input  read,
  output bus_0
);

  wire comparator_1_a___b;

  Comparator comparator_1 (.A(16'hdeb0), .B(addr_bus), .A___B(comparator_1_a___b));  // open: A___B_2, A___B_3
  and and_1 (bus_0, comparator_1_a___b, mem, ~read);  // AND_Gate
endmodule

module IN_CTRL (
  input  [15:0] addr_bus,
  input  mem,
  input  read,
  output bus_0
);

  wire comparator_1_a___b;

  Comparator comparator_1 (.A(16'hdeae), .B(addr_bus), .A___B(comparator_1_a___b));  // open: A___B_2, A___B_3
  and and_1 (bus_0, comparator_1_a___b, mem, read);
endmodule

module randctrl1 (
  input  [15:0] addr_bus,
  input  [15:0] data_bus,
  input  mem,
  input  read,
  input  clk,
  output [3:0] out
);

  wire and_1_out, comparator_1_a___b;
  wire [15:4] register_1_q;

  Comparator comparator_1 (.A(16'hff4c), .B(addr_bus), .A___B(comparator_1_a___b));  // open: A___B_2, A___B_3
  and and_1 (and_1_out, comparator_1_a___b, mem, ~read);  // AND_Gate
  Register #(.width(16)) register_1 (.D(data_bus), .en(and_1_out), .Q({register_1_q, out}), .clk(clk));  // open: clr
endmodule

module randctrl2 (
  input  [15:0] addr_bus,
  input  [15:0] data_bus,
  input  mem,
  input  read,
  input  clk,
  output [3:0] out
);

  wire and_1_out, comparator_1_a___b;
  wire [15:4] register_1_q;

  Comparator comparator_1 (.A(16'hff4d), .B(addr_bus), .A___B(comparator_1_a___b));  // open: A___B_2, A___B_3
  and and_1 (and_1_out, comparator_1_a___b, mem, ~read);  // AND_Gate
  Register #(.width(16)) register_1 (.D(data_bus), .en(and_1_out), .Q({register_1_q, out}), .clk(clk));  // open: clr
endmodule

module matrix_register_white (
  input  [15:0] DATA,
  input  column,
  input  column_num,
  input  write,
  input  clk,
  output [31:0] out_6
);

  wire and_1_out, and_2_out;
  wire [15:0] shifter_bot_white_1_out, shifter_top_white_1_out;

  shifter_bot_white shifter_bot_white_1 (.in(DATA), .out(shifter_bot_white_1_out));
  and and_1 (and_1_out, ~column, column_num, write);  // AND_Gate
  shifter_top_white shifter_top_white_1 (.in(DATA), .out(shifter_top_white_1_out));
  and and_2 (and_2_out, column, column_num, write);
  Register #(.width(16), .trigger("falling")) reg_top (
    .D(shifter_top_white_1_out), .en(and_2_out), .Q(out_6[31:16]), .clk(clk));  // open: clr
  Register #(.width(16), .trigger("falling")) reg_bot (
    .D(shifter_bot_white_1_out), .en(and_1_out), .Q(out_6[15:0]), .clk(clk));  // open: clr
endmodule

module matrix_register_black (
  input  [15:0] DATA,
  input  column,
  input  column_num,
  input  write,
  input  clk,
  output [31:0] out_6
);

  wire and_1_out, and_2_out;
  wire [15:0] shifter_bot_black_1_out, shifter_top_black_1_out;

  shifter_bot_black shifter_bot_black_1 (.in(DATA), .out(shifter_bot_black_1_out));
  and and_1 (and_1_out, ~column, column_num, write);  // AND_Gate
  shifter_top_black shifter_top_black_1 (.in(DATA), .out(shifter_top_black_1_out));
  and and_2 (and_2_out, column, column_num, write);
  Register #(.width(16), .trigger("falling")) reg_top (
    .D(shifter_top_black_1_out), .en(and_2_out), .Q(out_6[31:16]), .clk(clk));  // open: clr
  Register #(.width(16), .trigger("falling")) reg_bot (
    .D(shifter_bot_black_1_out), .en(and_1_out), .Q(out_6[15:0]), .clk(clk));  // open: clr
endmodule

module Comparator (
  input  [15:0] A,
  input  [15:0] B,
  output A___B,
  output A___B_2,
  output A___B_3
);

  wire n1bitcomp_1_eq_out, n1bitcomp_1_gt_out, n1bitcomp_1_lt_out, n1bitcomp_2_eq_out, n1bitcomp_2_gt_out,
       n1bitcomp_2_lt_out, n1bitcomp_3_eq_out, n1bitcomp_3_gt_out, n1bitcomp_3_lt_out, n1bitcomp_4_eq_out,
       n1bitcomp_4_gt_out, n1bitcomp_4_lt_out, n1bitcomp_5_eq_out, n1bitcomp_5_gt_out, n1bitcomp_5_lt_out,
       n1bitcomp_6_eq_out, n1bitcomp_6_gt_out, n1bitcomp_6_lt_out, n1bitcomp_7_eq_out, n1bitcomp_7_gt_out,
       n1bitcomp_7_lt_out, n1bitcomp_8_eq_out, n1bitcomp_8_gt_out, n1bitcomp_8_lt_out, n1bitcomp_9_eq_out,
       n1bitcomp_9_gt_out, n1bitcomp_9_lt_out, n1bitcomp_10_eq_out, n1bitcomp_10_gt_out, n1bitcomp_10_lt_out,
       n1bitcomp_11_eq_out, n1bitcomp_11_gt_out, n1bitcomp_11_lt_out, n1bitcomp_12_eq_out,
       n1bitcomp_12_gt_out, n1bitcomp_12_lt_out, n1bitcomp_13_eq_out, n1bitcomp_13_gt_out,
       n1bitcomp_13_lt_out, n1bitcomp_14_eq_out, n1bitcomp_14_gt_out, n1bitcomp_14_lt_out,
       n1bitcomp_15_eq_out, n1bitcomp_15_gt_out, n1bitcomp_15_lt_out;

  _1BitComp u_1bitcomp_1 (
    .EQ_in(1'b1), .A_bit(A[15]), .B_bit(B[15]), .GT_in(1'b0), .LT_in(1'b0), .EQ_out(n1bitcomp_1_eq_out),
    .GT_out(n1bitcomp_1_gt_out), .LT_out(n1bitcomp_1_lt_out));
  _1BitComp u_1bitcomp_2 (
    .EQ_in(n1bitcomp_1_eq_out), .A_bit(A[14]), .B_bit(B[14]), .GT_in(n1bitcomp_1_gt_out),
    .LT_in(n1bitcomp_1_lt_out), .EQ_out(n1bitcomp_2_eq_out), .GT_out(n1bitcomp_2_gt_out),
    .LT_out(n1bitcomp_2_lt_out));
  _1BitComp u_1bitcomp_3 (
    .EQ_in(n1bitcomp_2_eq_out), .A_bit(A[13]), .B_bit(B[13]), .GT_in(n1bitcomp_2_gt_out),
    .LT_in(n1bitcomp_2_lt_out), .EQ_out(n1bitcomp_3_eq_out), .GT_out(n1bitcomp_3_gt_out),
    .LT_out(n1bitcomp_3_lt_out));
  _1BitComp u_1bitcomp_4 (
    .EQ_in(n1bitcomp_3_eq_out), .A_bit(A[12]), .B_bit(B[12]), .GT_in(n1bitcomp_3_gt_out),
    .LT_in(n1bitcomp_3_lt_out), .EQ_out(n1bitcomp_4_eq_out), .GT_out(n1bitcomp_4_gt_out),
    .LT_out(n1bitcomp_4_lt_out));
  _1BitComp u_1bitcomp_5 (
    .EQ_in(n1bitcomp_4_eq_out), .A_bit(A[11]), .B_bit(B[11]), .GT_in(n1bitcomp_4_gt_out),
    .LT_in(n1bitcomp_4_lt_out), .EQ_out(n1bitcomp_5_eq_out), .GT_out(n1bitcomp_5_gt_out),
    .LT_out(n1bitcomp_5_lt_out));
  _1BitComp u_1bitcomp_6 (
    .EQ_in(n1bitcomp_5_eq_out), .A_bit(A[10]), .B_bit(B[10]), .GT_in(n1bitcomp_5_gt_out),
    .LT_in(n1bitcomp_5_lt_out), .EQ_out(n1bitcomp_6_eq_out), .GT_out(n1bitcomp_6_gt_out),
    .LT_out(n1bitcomp_6_lt_out));
  _1BitComp u_1bitcomp_7 (
    .EQ_in(n1bitcomp_6_eq_out), .A_bit(A[9]), .B_bit(B[9]), .GT_in(n1bitcomp_6_gt_out),
    .LT_in(n1bitcomp_6_lt_out), .EQ_out(n1bitcomp_7_eq_out), .GT_out(n1bitcomp_7_gt_out),
    .LT_out(n1bitcomp_7_lt_out));
  _1BitComp u_1bitcomp_8 (
    .EQ_in(n1bitcomp_7_eq_out), .A_bit(A[8]), .B_bit(B[8]), .GT_in(n1bitcomp_7_gt_out),
    .LT_in(n1bitcomp_7_lt_out), .EQ_out(n1bitcomp_8_eq_out), .GT_out(n1bitcomp_8_gt_out),
    .LT_out(n1bitcomp_8_lt_out));
  _1BitComp u_1bitcomp_9 (
    .EQ_in(n1bitcomp_8_eq_out), .A_bit(A[7]), .B_bit(B[7]), .GT_in(n1bitcomp_8_gt_out),
    .LT_in(n1bitcomp_8_lt_out), .EQ_out(n1bitcomp_9_eq_out), .GT_out(n1bitcomp_9_gt_out),
    .LT_out(n1bitcomp_9_lt_out));
  _1BitComp u_1bitcomp_10 (
    .EQ_in(n1bitcomp_9_eq_out), .A_bit(A[6]), .B_bit(B[6]), .GT_in(n1bitcomp_9_gt_out),
    .LT_in(n1bitcomp_9_lt_out), .EQ_out(n1bitcomp_10_eq_out), .GT_out(n1bitcomp_10_gt_out),
    .LT_out(n1bitcomp_10_lt_out));
  _1BitComp u_1bitcomp_11 (
    .EQ_in(n1bitcomp_10_eq_out), .A_bit(A[5]), .B_bit(B[5]), .GT_in(n1bitcomp_10_gt_out),
    .LT_in(n1bitcomp_10_lt_out), .EQ_out(n1bitcomp_11_eq_out), .GT_out(n1bitcomp_11_gt_out),
    .LT_out(n1bitcomp_11_lt_out));
  _1BitComp u_1bitcomp_12 (
    .EQ_in(n1bitcomp_11_eq_out), .A_bit(A[4]), .B_bit(B[4]), .GT_in(n1bitcomp_11_gt_out),
    .LT_in(n1bitcomp_11_lt_out), .EQ_out(n1bitcomp_12_eq_out), .GT_out(n1bitcomp_12_gt_out),
    .LT_out(n1bitcomp_12_lt_out));
  _1BitComp u_1bitcomp_13 (
    .EQ_in(n1bitcomp_12_eq_out), .A_bit(A[3]), .B_bit(B[3]), .GT_in(n1bitcomp_12_gt_out),
    .LT_in(n1bitcomp_12_lt_out), .EQ_out(n1bitcomp_13_eq_out), .GT_out(n1bitcomp_13_gt_out),
    .LT_out(n1bitcomp_13_lt_out));
  _1BitComp u_1bitcomp_14 (
    .EQ_in(n1bitcomp_13_eq_out), .A_bit(A[2]), .B_bit(B[2]), .GT_in(n1bitcomp_13_gt_out),
    .LT_in(n1bitcomp_13_lt_out), .EQ_out(n1bitcomp_14_eq_out), .GT_out(n1bitcomp_14_gt_out),
    .LT_out(n1bitcomp_14_lt_out));
  _1BitComp u_1bitcomp_15 (
    .EQ_in(n1bitcomp_14_eq_out), .A_bit(A[1]), .B_bit(B[1]), .GT_in(n1bitcomp_14_gt_out),
    .LT_in(n1bitcomp_14_lt_out), .EQ_out(n1bitcomp_15_eq_out), .GT_out(n1bitcomp_15_gt_out),
    .LT_out(n1bitcomp_15_lt_out));
  _1BitComp u_1bitcomp_16 (
    .EQ_in(n1bitcomp_15_eq_out), .A_bit(A[0]), .B_bit(B[0]), .GT_in(n1bitcomp_15_gt_out),
    .LT_in(n1bitcomp_15_lt_out), .EQ_out(A___B), .GT_out(A___B_2), .LT_out(A___B_3));
endmodule

module _1BitComp (
  input  EQ_in,
  input  A_bit,
  input  B_bit,
  input  GT_in,
  input  LT_in,
  output EQ_out,
  output GT_out,
  output LT_out
);

  wire and_1_out, and_2_out, and_4_out, and_5_out, xnor_1_out;

  and and_1 (and_1_out, A_bit, ~B_bit);  // AND_Gate
  and and_2 (and_2_out, ~A_bit, B_bit);  // AND_Gate
  xnor xnor_1 (xnor_1_out, A_bit, B_bit);
  and and_3 (EQ_out, EQ_in, xnor_1_out);
  and and_4 (and_4_out, EQ_in, and_1_out);
  and and_5 (and_5_out, EQ_in, and_2_out);
  or or_1 (GT_out, and_4_out, GT_in);
  or or_2 (LT_out, and_5_out, LT_in);
endmodule
